# Fritzing sketch sketch (saved by Fritzing 0.9.1b)
breadboards: 1

parts:
  Part1 = Arduino Uno (Rev3)
  R5 = Resistor [tolerance=±5% resistance=220 package=THT]
  R6 = Resistor [tolerance=±5% resistance=220 package=THT]
  LED1 = LED - 3mm [color="Red (633nm)" package="3 mm [THT]"]
  R7 = Resistor [tolerance=±5% resistance=220 package=THT]
  R8 = Resistor [tolerance=±5% resistance=220 package=THT]
  R9 = Resistor [tolerance=±5% resistance=220 package=THT]
  R10 = Resistor [tolerance=±5% resistance=220 package=THT]
  LED2 = LED - 3mm [color="Red (633nm)" package="3 mm [THT]"]
  LED3 = LED - 3mm [color="Red (633nm)" package="3 mm [THT]"]
  LED4 = LED - 3mm [color="Red (633nm)" package="3 mm [THT]"]
  R11 = Rotary Potentiometer (Small) [maximum_resistance=100kΩ package=THT]
  LED5 = LED - 3mm [color="Red (633nm)" package="3 mm [THT]"]
  LED6 = LED - 3mm [color="Red (633nm)" package="3 mm [THT]"]

nets:
  N1: Part1.A0, R11.wiper
  N2: Part1.D8, R6.Pin_0
  N3: Part1.D9_PWM, R5.Pin_0
  N4: Part1.D10_PWM/SS, R7.Pin_0
  N5: Part1.D11_PWM/MOSI, R8.Pin_0
  N6: Part1.D12/MISO, R9.Pin_0
  N7: Part1.D13/SCK, R10.Pin_0
  N8: Part1.GND, LED1.cathode, LED2.cathode, LED3.cathode, LED4.cathode, R11.leg1, R11.leg2, LED5.cathode, LED6.cathode
  N9: R5.Pin_1, LED5.anode
  N10: R6.Pin_1, LED6.anode
  N11: LED1.anode, R7.Pin_1
  N12: R8.Pin_1, LED2.anode
  N13: R9.Pin_1, LED3.anode
  N14: R10.Pin_1, LED4.anode

// code stored in the sketch: codigo.ino

//Definir los pines de donde conectaremos los leds
byte ledPin[] = {8, 9, 10, 11, 12, 13};

long timeChanged = 0;
//Velocidad inicial
int delayTime = 200;
int currentLED = 0;
//Variable que controla la direccion
int dir = 1;
//Setup
void setup() {
  //Puerto para enviar datos (para escribir lo que esta pasando)
  Serial.begin(9600);
  for (int i=0; i<6; i++) {
      pinMode(ledPin[i], OUTPUT);
    } 
   timeChanged = millis();
}
//Loop
void loop() {

    //Definimos cuando se ejecuta el cambio de luz
    if ((millis() - timeChanged) > delayTime) { 
      
      for (int i=0; i<6; i++) {
        digitalWrite(ledPin[i], LOW);
      }   
      digitalWrite(ledPin[currentLED], HIGH); 
      currentLED = currentLED + dir;      
      if (currentLED ==5) {
        dir=-1;
      }
      if(currentLED ==0){
        dir=1;
      }
      timeChanged = millis();
    }
    //Leemos el potenciometro
    delayTime= analogRead(0);
    Serial.println("Velocidad ");
     Serial.println(delayTime);
    
    delay(5);
    
}
